// Logisim project 4-bitALU.circ as structural Verilog: 22 circuits, main circuit main
module main (
  input  [3:0] opcode,
  input  carry_in,
  input  [7:0] A,
  input  [7:0] B,
  output A_B,
  output A_B_2,
  output A_B_3,
  output [7:0] out_8,
  output CARRY_OUT
);

  wire ADDER_carry_out, DECREMENT_carry, INCREMENT_carry, LEFT_SHIFT_fall_off, RIGHT_SHIFT_fall_off;
  wire [7:0] ADDER_results, AND_results, DECREMENT_results, INCREMENT_results, LEFT_SHIFT_results,
       NOT_results, OR_results, RIGHT_SHIFT_results;

  _8_bit_ADDER ADDER (.A(A), .B(B), .Results(ADDER_results), .carry_out(ADDER_carry_out));
  _8_bit_IMCREMENT INCREMENT (
    .A___B_SWITCH(opcode[1]), .A(A), .B(B), .Results(INCREMENT_results), .CARRY(INCREMENT_carry));
  _8_bit_DECREMENT DECREMENT (
    .A___B_SWITCH(opcode[2]), .A(A), .B(B), .Results(DECREMENT_results), .CARRY(DECREMENT_carry));
  _8_bit_NOT NOT (.not_A__not_B_control(opcode[0]), .B(B), .A(A), .Results(NOT_results));
  _8_bit_AND AND (.B(B), .A(A), .Results(AND_results));
  _8_bit_OR OR (.B(B), .A(A), .Results(OR_results));
  _8_bit_RIGHT_SHIFT RIGHT_SHIFT (
    .CARRY_IN(carry_in), .A___B_SWITCH(opcode[0]), .A(A), .B(B), .FALL_OFF(RIGHT_SHIFT_fall_off),
    .Results(RIGHT_SHIFT_results));
  _8_bit_LEFT_SHIFT LEFT_SHIFT (
    .CARRY_IN(carry_in), .A___B_SWITCH(opcode[0]), .A(A), .B(B), .Results(LEFT_SHIFT_results),
    .FALL_OFF(LEFT_SHIFT_fall_off));
  Multiplexer #(.select(4), .width(8)) multiplexer_1 (
    .in0(ADDER_results), .in1(INCREMENT_results), .in2(INCREMENT_results), .in3(DECREMENT_results),
    .in4(DECREMENT_results), .in6(NOT_results), .in7(NOT_results), .in8(AND_results), .in9(OR_results),
    .in10(RIGHT_SHIFT_results), .in11(RIGHT_SHIFT_results), .in12(LEFT_SHIFT_results),
    .in13(LEFT_SHIFT_results), .out(out_8), .sel(opcode));  // open: in5, in14, in15, en
  Multiplexer #(.select(4)) multiplexer_2 (
    .in0(ADDER_carry_out), .in1(INCREMENT_carry), .in2(INCREMENT_carry), .in3(DECREMENT_carry),
    .in4(DECREMENT_carry), .in10(RIGHT_SHIFT_fall_off), .in11(RIGHT_SHIFT_fall_off),
    .in12(LEFT_SHIFT_fall_off), .in13(LEFT_SHIFT_fall_off), .out(CARRY_OUT), .sel(opcode));  // open: in5, in6, in7, in8, in9, in14, in15, en
  Comparator comparator_1 (.a(A), .b(B), .gt(A_B), .eq(A_B_2), .lt(A_B_3));
endmodule

module _4_bit_adder_subtractor (
  input  Add_Subtract_control,
  input  [3:0] A,
  input  [3:0] B,
  output [3:0] Results,
  output carry_out,
  output overflow
);

  wire and_1_out, and_2_out, full_adder_1_out, full_adder_2_out, full_adder_3_out, not_1_out, not_2_out,
       not_3_out, xor_1_out, xor_2_out, xor_3_out, xor_4_out;

  xor xor_1 (xor_1_out, Add_Subtract_control, B[0]);
  xor xor_2 (xor_2_out, Add_Subtract_control, B[1]);
  xor xor_3 (xor_3_out, Add_Subtract_control, B[2]);
  xor xor_4 (xor_4_out, Add_Subtract_control, B[3]);
  not not_1 (not_1_out, xor_4_out);
  not not_2 (not_2_out, A[3]);
  Full_adder full_adder_1 (
    .A(A[0]), .B(xor_1_out), .in(Add_Subtract_control), .out(full_adder_1_out), .Result(Results[0]));
  Full_adder full_adder_2 (.A(A[1]), .B(xor_2_out), .in(full_adder_1_out), .out(full_adder_2_out), .Result(Results[1]));
  Full_adder full_adder_3 (.A(A[2]), .B(xor_3_out), .in(full_adder_2_out), .out(full_adder_3_out), .Result(Results[2]));
  Full_adder full_adder_4 (.A(A[3]), .B(xor_4_out), .in(full_adder_3_out), .out(carry_out), .Result(Results[3]));
  not not_3 (not_3_out, Results[3]);
  and and_1 (and_1_out, Results[3], not_2_out, not_1_out);
  and and_2 (and_2_out, not_3_out, A[3], xor_4_out);
  or or_1 (overflow, and_1_out, and_2_out);
endmodule

module _4_bit_and (
  input  [3:0] A,
  input  [3:0] B,
  output [3:0] Results
);

  and and_1 (Results[0], A[0], B[0]);
  and and_2 (Results[1], A[1], B[1]);
  and and_3 (Results[2], A[2], B[2]);
  and and_4 (Results[3], A[3], B[3]);
endmodule

module _4_bit_or (
  input  [3:0] A,
  input  [3:0] B,
  output [3:0] Results
);

  or or_1 (Results[0], A[0], B[0]);
  or or_2 (Results[1], A[1], B[1]);
  or or_3 (Results[2], A[2], B[2]);
  or or_4 (Results[3], A[3], B[3]);
endmodule

module _4bit_example (
  input  [3:0] A,
  input  [3:0] B,
  input  _0,
  input  _1,
  input  [7:0] A_2,
  input  [7:0] A_3,
  output [3:0] out_7,
  output ZERO,
  output NEGATIVE,
  output CARRY,
  output OVERFLOW
);

  wire or_2_out;
  wire [3:0] ADD_SUB_results, AND_results, multiplexer_1_out, OR_results;

  _4_bit_and AND (.B(B), .A(A), .Results(AND_results));
  _4_bit_or OR (.B(B), .A(A), .Results(OR_results));
  _4_bit_adder_subtractor ADD_SUB (
    .Add_Subtract_control(_0), .A(A), .B(B), .Results(ADD_SUB_results), .carry_out(CARRY), .overflow(OVERFLOW));
  Multiplexer #(.width(4)) multiplexer_1 (
    .in0(AND_results), .in1(OR_results), .out(multiplexer_1_out), .sel(_0));  // open: en
  Multiplexer #(.width(4)) multiplexer_2 (
    .in0(multiplexer_1_out), .in1(ADD_SUB_results), .out({NEGATIVE, out_7[2:0]}), .sel(_1));  // open: en
  or or_2 (or_2_out, out_7[0], out_7[1], out_7[2], NEGATIVE);
  not not_1 (ZERO, or_2_out);

  assign A_3 = A_2;
  assign out_7[3] = NEGATIVE;
endmodule

// FULL ADDER
module Full_adder (
  input  in,
  input  A,
  input  B,
  output Result,
  output out
);

  wire and_1_out, and_2_out, xor_1_out;

  and and_1 (and_1_out, A, B);
  xor xor_1 (xor_1_out, A, B);
  or or_1 (out, and_1_out, and_2_out);
  and and_2 (and_2_out, in, xor_1_out);
  xor xor_2 (Result, in, xor_1_out);
endmodule

// FULL SUBTRACTOR
module full_subtractor (
  input  in,
  input  A,
  input  B,
  output Result,
  output out
);

  wire and_1_out, and_2_out, not_1_out, not_2_out, xor_1_out;

  not not_1 (not_1_out, A);
  and and_1 (and_1_out, not_1_out, B);
  xor xor_1 (xor_1_out, A, B);
  or or_1 (out, and_1_out, and_2_out);
  not not_2 (not_2_out, xor_1_out);
  and and_2 (and_2_out, not_2_out, in);
  xor xor_2 (Result, in, xor_1_out);
endmodule

// HALF ADDER
module half_adder (
  input  A,
  input  B,
  output SUM,
  output CARRY
);

  xor xor_1 (SUM, A, B);
  and and_1 (CARRY, B, A);
endmodule

// HALF SUBTRACTOR
module half_subtractor (
  input  A,
  input  B,
  output SUM,
  output CARRY
);

  wire not_1_out;

  not not_1 (not_1_out, A);
  xor xor_1 (SUM, A, B);
  and and_1 (CARRY, B, not_1_out);
endmodule

// MULTIOLEXER
module MULTIPLEXER (
  input  SELECTOR,
  input  A,
  input  B,
  output OUTPUT
);

  wire nand_1_out, nand_2_out, not_1_out;

  not not_1 (not_1_out, SELECTOR);
  nand nand_1 (nand_1_out, not_1_out, A);
  nand nand_2 (nand_2_out, SELECTOR, B);
  nand nand_3 (OUTPUT, nand_1_out, nand_2_out);
endmodule

module D_Type_Flip_Flop (
  input  D,
  input  E,
  output Q,
  output nQ
);

  wire nand_1_out, nand_2_out;

  nand nand_1 (nand_1_out, D, E);
  nand nand_2 (nand_2_out, nand_1_out, E);
  nand nand_3 (Q, nand_1_out, nQ);
  nand nand_4 (nQ, Q, nand_2_out);
endmodule

module _8_bit_adder_subtractor (
  input  Add_Subtract_control,
  input  [7:0] A,
  input  [7:0] B,
  output [7:0] Results,
  output carry_out
);

  wire full_adder_1_out, full_adder_2_out, full_adder_3_out, full_adder_4_out, full_adder_5_out,
       full_adder_6_out, full_adder_7_out, xor_1_out, xor_2_out, xor_3_out, xor_4_out, xor_5_out, xor_6_out,
       xor_7_out, xor_8_out;

  xor xor_1 (xor_1_out, Add_Subtract_control, B[0]);
  xor xor_2 (xor_2_out, Add_Subtract_control, B[1]);
  xor xor_3 (xor_3_out, Add_Subtract_control, B[2]);
  xor xor_4 (xor_4_out, Add_Subtract_control, B[3]);
  xor xor_5 (xor_5_out, Add_Subtract_control, B[4]);
  xor xor_6 (xor_6_out, Add_Subtract_control, B[5]);
  xor xor_7 (xor_7_out, Add_Subtract_control, B[6]);
  xor xor_8 (xor_8_out, Add_Subtract_control, B[7]);
  Full_adder full_adder_1 (
    .A(A[0]), .B(xor_1_out), .in(Add_Subtract_control), .out(full_adder_1_out), .Result(Results[0]));
  Full_adder full_adder_2 (.A(A[1]), .B(xor_2_out), .in(full_adder_1_out), .out(full_adder_2_out), .Result(Results[1]));
  Full_adder full_adder_3 (.A(A[2]), .B(xor_3_out), .in(full_adder_2_out), .out(full_adder_3_out), .Result(Results[2]));
  Full_adder full_adder_4 (.A(A[3]), .B(xor_4_out), .in(full_adder_3_out), .out(full_adder_4_out), .Result(Results[3]));
  Full_adder full_adder_5 (.A(A[4]), .B(xor_5_out), .in(full_adder_4_out), .out(full_adder_5_out), .Result(Results[4]));
  Full_adder full_adder_6 (.A(A[5]), .B(xor_6_out), .in(full_adder_5_out), .out(full_adder_6_out), .Result(Results[5]));
  Full_adder full_adder_7 (.A(A[6]), .B(xor_7_out), .in(full_adder_6_out), .out(full_adder_7_out), .Result(Results[6]));
  Full_adder full_adder_8 (.A(A[7]), .B(xor_8_out), .in(full_adder_7_out), .out(carry_out), .Result(Results[7]));
endmodule

module _8_bit_ADDER (
  input  [7:0] A,
  input  [7:0] B,
  output [7:0] Results,
  output carry_out
);

  wire full_adder_1_out, full_adder_2_out, full_adder_3_out, full_adder_4_out, full_adder_5_out,
       full_adder_6_out, half_adder_1_carry;

  half_adder half_adder_1 (.A(A[0]), .B(B[0]), .SUM(Results[0]), .CARRY(half_adder_1_carry));
  Full_adder full_adder_1 (.A(A[1]), .B(B[1]), .in(half_adder_1_carry), .out(full_adder_1_out), .Result(Results[1]));
  Full_adder full_adder_2 (.A(A[2]), .B(B[2]), .in(full_adder_1_out), .out(full_adder_2_out), .Result(Results[2]));
  Full_adder full_adder_3 (.A(A[3]), .B(B[3]), .in(full_adder_2_out), .out(full_adder_3_out), .Result(Results[3]));
  Full_adder full_adder_4 (.A(A[4]), .B(B[4]), .in(full_adder_3_out), .out(full_adder_4_out), .Result(Results[4]));
  Full_adder full_adder_5 (.A(A[5]), .B(B[5]), .in(full_adder_4_out), .out(full_adder_5_out), .Result(Results[5]));
  Full_adder full_adder_6 (.A(A[6]), .B(B[6]), .in(full_adder_5_out), .out(full_adder_6_out), .Result(Results[6]));
  Full_adder full_adder_7 (.A(A[7]), .B(B[7]), .in(full_adder_6_out), .out(carry_out), .Result(Results[7]));
endmodule

module _8_bit_SUBTRACT (
  input  [7:0] A,
  input  [7:0] B,
  output [7:0] Results,
  output carry_out
);

  wire full_subtractor_1_out, full_subtractor_2_out, full_subtractor_3_out, full_subtractor_4_out,
       full_subtractor_5_out, full_subtractor_6_out, half_subtractor_1_carry;

  half_subtractor half_subtractor_1 (.A(A[0]), .B(B[0]), .SUM(Results[0]), .CARRY(half_subtractor_1_carry));
  full_subtractor full_subtractor_1 (
    .A(A[1]), .B(B[1]), .in(half_subtractor_1_carry), .out(full_subtractor_1_out), .Result(Results[1]));
  full_subtractor full_subtractor_2 (
    .A(A[2]), .B(B[2]), .in(full_subtractor_1_out), .out(full_subtractor_2_out), .Result(Results[2]));
  full_subtractor full_subtractor_3 (
    .A(A[3]), .B(B[3]), .in(full_subtractor_2_out), .out(full_subtractor_3_out), .Result(Results[3]));
  full_subtractor full_subtractor_4 (
    .A(A[4]), .B(B[4]), .in(full_subtractor_3_out), .out(full_subtractor_4_out), .Result(Results[4]));
  full_subtractor full_subtractor_5 (
    .A(A[5]), .B(B[5]), .in(full_subtractor_4_out), .out(full_subtractor_5_out), .Result(Results[5]));
  full_subtractor full_subtractor_6 (
    .A(A[6]), .B(B[6]), .in(full_subtractor_5_out), .out(full_subtractor_6_out), .Result(Results[6]));
  full_subtractor full_subtractor_7 (
    .A(A[7]), .B(B[7]), .in(full_subtractor_6_out), .out(carry_out), .Result(Results[7]));
endmodule

module _8_bit_IMCREMENT (
  input  A___B_SWITCH,
  input  [7:0] A,
  input  [7:0] B,
  output [7:0] Results,
  output CARRY
);

  wire half_adder_1_carry, half_adder_2_carry, half_adder_3_carry, half_adder_4_carry, half_adder_5_carry,
       half_adder_6_carry, half_adder_7_carry, multiplexer_1_output, multiplexer_2_output,
       multiplexer_3_output, multiplexer_4_output, multiplexer_5_output, multiplexer_6_output,
       multiplexer_7_output, multiplexer_8_output;

  MULTIPLEXER multiplexer_1 (.SELECTOR(A___B_SWITCH), .A(A[0]), .B(B[0]), .OUTPUT(multiplexer_1_output));
  MULTIPLEXER multiplexer_2 (.SELECTOR(A___B_SWITCH), .A(A[1]), .B(B[1]), .OUTPUT(multiplexer_2_output));
  MULTIPLEXER multiplexer_3 (.SELECTOR(A___B_SWITCH), .A(A[2]), .B(B[2]), .OUTPUT(multiplexer_3_output));
  MULTIPLEXER multiplexer_4 (.SELECTOR(A___B_SWITCH), .A(A[3]), .B(B[3]), .OUTPUT(multiplexer_4_output));
  MULTIPLEXER multiplexer_5 (.SELECTOR(A___B_SWITCH), .A(A[4]), .B(B[4]), .OUTPUT(multiplexer_5_output));
  MULTIPLEXER multiplexer_6 (.SELECTOR(A___B_SWITCH), .A(A[5]), .B(B[5]), .OUTPUT(multiplexer_6_output));
  MULTIPLEXER multiplexer_7 (.SELECTOR(A___B_SWITCH), .A(A[6]), .B(B[6]), .OUTPUT(multiplexer_7_output));
  MULTIPLEXER multiplexer_8 (.SELECTOR(A___B_SWITCH), .A(A[7]), .B(B[7]), .OUTPUT(multiplexer_8_output));
  half_adder half_adder_1 (.A(multiplexer_1_output), .B(1'b1), .SUM(Results[0]), .CARRY(half_adder_1_carry));
  half_adder half_adder_2 (
    .A(multiplexer_2_output), .B(half_adder_1_carry), .SUM(Results[1]), .CARRY(half_adder_2_carry));
  half_adder half_adder_3 (
    .A(multiplexer_3_output), .B(half_adder_2_carry), .SUM(Results[2]), .CARRY(half_adder_3_carry));
  half_adder half_adder_4 (
    .A(multiplexer_4_output), .B(half_adder_3_carry), .SUM(Results[3]), .CARRY(half_adder_4_carry));
  half_adder half_adder_5 (
    .A(multiplexer_5_output), .B(half_adder_4_carry), .SUM(Results[4]), .CARRY(half_adder_5_carry));
  half_adder half_adder_6 (
    .A(multiplexer_6_output), .B(half_adder_5_carry), .SUM(Results[5]), .CARRY(half_adder_6_carry));
  half_adder half_adder_7 (
    .A(multiplexer_7_output), .B(half_adder_6_carry), .SUM(Results[6]), .CARRY(half_adder_7_carry));
  half_adder half_adder_8 (.A(multiplexer_8_output), .B(half_adder_7_carry), .SUM(Results[7]), .CARRY(CARRY));
endmodule

module _8_bit_DECREMENT (
  input  A___B_SWITCH,
  input  [7:0] A,
  input  [7:0] B,
  output [7:0] Results,
  output CARRY
);

  wire half_subtractor_1_carry, half_subtractor_2_carry, half_subtractor_3_carry, half_subtractor_4_carry,
       half_subtractor_5_carry, half_subtractor_6_carry, half_subtractor_7_carry, multiplexer_1_output,
       multiplexer_2_output, multiplexer_3_output, multiplexer_4_output, multiplexer_5_output,
       multiplexer_6_output, multiplexer_7_output, multiplexer_8_output;

  MULTIPLEXER multiplexer_1 (.SELECTOR(A___B_SWITCH), .A(A[0]), .B(B[0]), .OUTPUT(multiplexer_1_output));
  MULTIPLEXER multiplexer_2 (.SELECTOR(A___B_SWITCH), .A(A[1]), .B(B[1]), .OUTPUT(multiplexer_2_output));
  MULTIPLEXER multiplexer_3 (.SELECTOR(A___B_SWITCH), .A(A[2]), .B(B[2]), .OUTPUT(multiplexer_3_output));
  MULTIPLEXER multiplexer_4 (.SELECTOR(A___B_SWITCH), .A(A[3]), .B(B[3]), .OUTPUT(multiplexer_4_output));
  MULTIPLEXER multiplexer_5 (.SELECTOR(A___B_SWITCH), .A(A[4]), .B(B[4]), .OUTPUT(multiplexer_5_output));
  MULTIPLEXER multiplexer_6 (.SELECTOR(A___B_SWITCH), .A(A[5]), .B(B[5]), .OUTPUT(multiplexer_6_output));
  MULTIPLEXER multiplexer_7 (.SELECTOR(A___B_SWITCH), .A(A[6]), .B(B[6]), .OUTPUT(multiplexer_7_output));
  MULTIPLEXER multiplexer_8 (.SELECTOR(A___B_SWITCH), .A(A[7]), .B(B[7]), .OUTPUT(multiplexer_8_output));
  half_subtractor half_subtractor_1 (
    .A(multiplexer_1_output), .B(1'b1), .SUM(Results[0]), .CARRY(half_subtractor_1_carry));
  half_subtractor half_subtractor_2 (
    .A(multiplexer_2_output), .B(half_subtractor_1_carry), .SUM(Results[1]), .CARRY(half_subtractor_2_carry));
  half_subtractor half_subtractor_3 (
    .A(multiplexer_3_output), .B(half_subtractor_2_carry), .SUM(Results[2]), .CARRY(half_subtractor_3_carry));
  half_subtractor half_subtractor_4 (
    .A(multiplexer_4_output), .B(half_subtractor_3_carry), .SUM(Results[3]), .CARRY(half_subtractor_4_carry));
  half_subtractor half_subtractor_5 (
    .A(multiplexer_5_output), .B(half_subtractor_4_carry), .SUM(Results[4]), .CARRY(half_subtractor_5_carry));
  half_subtractor half_subtractor_6 (
    .A(multiplexer_6_output), .B(half_subtractor_5_carry), .SUM(Results[5]), .CARRY(half_subtractor_6_carry));
  half_subtractor half_subtractor_7 (
    .A(multiplexer_7_output), .B(half_subtractor_6_carry), .SUM(Results[6]), .CARRY(half_subtractor_7_carry));
  half_subtractor half_subtractor_8 (
    .A(multiplexer_8_output), .B(half_subtractor_7_carry), .SUM(Results[7]), .CARRY(CARRY));
endmodule

module _8_bit_COMPARISON (
  input  [7:0] A,
  input  [7:0] B,
  output A_B,
  output A_B_2,
  output A_B_3
);

  wire and_1_out, and_2_out, and_3_out, and_4_out, and_5_out, and_6_out, and_7_out, and_8_out, and_9_out,
       and_10_out, and_11_out, and_12_out, and_13_out, and_14_out, and_15_out, and_16_out, and_18_out,
       and_19_out, and_20_out, and_21_out, and_22_out, and_23_out, and_24_out, and_25_out, and_26_out,
       and_27_out, and_28_out, and_29_out, and_30_out, and_31_out, nor_1_out, nor_2_out, nor_3_out,
       nor_4_out, nor_5_out, nor_6_out, nor_7_out, nor_8_out, not_1_out, not_2_out, not_3_out, not_4_out,
       not_5_out, not_6_out, not_7_out, not_8_out, not_9_out, not_10_out, not_11_out, not_12_out, not_13_out,
       not_14_out, not_15_out, not_16_out;

  not not_1 (not_1_out, A[0]);
  not not_2 (not_2_out, B[0]);
  not not_3 (not_3_out, A[1]);
  not not_4 (not_4_out, B[1]);
  not not_5 (not_5_out, A[2]);
  not not_6 (not_6_out, B[2]);
  not not_7 (not_7_out, A[3]);
  not not_8 (not_8_out, B[3]);
  not not_9 (not_9_out, A[4]);
  not not_10 (not_10_out, B[4]);
  not not_11 (not_11_out, A[5]);
  not not_12 (not_12_out, B[5]);
  not not_13 (not_13_out, A[6]);
  not not_14 (not_14_out, B[6]);
  not not_15 (not_15_out, A[7]);
  not not_16 (not_16_out, B[7]);
  and and_1 (and_1_out, not_1_out, B[0]);
  and and_2 (and_2_out, not_2_out, A[0]);
  and and_3 (and_3_out, not_3_out, B[1]);
  and and_4 (and_4_out, not_4_out, A[1]);
  and and_5 (and_5_out, not_5_out, B[2]);
  and and_6 (and_6_out, not_6_out, A[2]);
  and and_7 (and_7_out, not_7_out, B[3]);
  and and_8 (and_8_out, not_8_out, A[3]);
  and and_9 (and_9_out, not_9_out, B[4]);
  and and_10 (and_10_out, not_10_out, A[4]);
  and and_11 (and_11_out, not_11_out, B[5]);
  and and_12 (and_12_out, not_12_out, A[5]);
  and and_13 (and_13_out, not_13_out, B[6]);
  and and_14 (and_14_out, not_14_out, A[6]);
  and and_15 (and_15_out, not_15_out, B[7]);
  and and_16 (and_16_out, not_16_out, A[7]);
  nor nor_1 (nor_1_out, and_1_out, and_2_out);
  nor nor_2 (nor_2_out, and_3_out, and_4_out);
  nor nor_3 (nor_3_out, and_5_out, and_6_out);
  nor nor_4 (nor_4_out, and_7_out, and_8_out);
  nor nor_5 (nor_5_out, and_9_out, and_10_out);
  nor nor_6 (nor_6_out, and_11_out, and_12_out);
  nor nor_7 (nor_7_out, and_13_out, and_14_out);
  nor nor_8 (nor_8_out, and_15_out, and_16_out);
  and and_17 (A_B, nor_1_out, nor_2_out, nor_3_out, nor_4_out, nor_5_out, nor_6_out, nor_7_out, nor_8_out);
  and and_18 (and_18_out, and_2_out, nor_2_out, nor_3_out, nor_4_out, nor_5_out, nor_6_out, nor_7_out, nor_8_out);
  and and_19 (and_19_out, and_1_out, nor_2_out, nor_3_out, nor_4_out, nor_5_out, nor_6_out, nor_7_out, nor_8_out);
  and and_20 (and_20_out, and_4_out, nor_3_out, nor_4_out, nor_5_out, nor_6_out, nor_7_out, nor_8_out);
  and and_21 (and_21_out, and_3_out, nor_3_out, nor_4_out, nor_5_out, nor_6_out, nor_7_out, nor_8_out);
  and and_22 (and_22_out, and_6_out, nor_4_out, nor_5_out, nor_6_out, nor_7_out, nor_8_out);
  and and_23 (and_23_out, and_5_out, nor_4_out, nor_5_out, nor_6_out, nor_7_out, nor_8_out);
  and and_24 (and_24_out, and_8_out, nor_5_out, nor_6_out, nor_7_out, nor_8_out);
  and and_25 (and_25_out, and_7_out, nor_5_out, nor_6_out, nor_7_out, nor_8_out);
  and and_26 (and_26_out, and_10_out, nor_6_out, nor_7_out, nor_8_out);
  and and_27 (and_27_out, and_9_out, nor_6_out, nor_7_out, nor_8_out);
  and and_28 (and_28_out, and_12_out, nor_7_out, nor_8_out);
  and and_29 (and_29_out, and_11_out, nor_7_out, nor_8_out);
  and and_30 (and_30_out, and_14_out, nor_8_out);
  and and_31 (and_31_out, and_13_out, nor_8_out);
  or or_1 (A_B_2, and_19_out, and_21_out, and_23_out, and_25_out, and_27_out, and_29_out, and_31_out, and_16_out);
  or or_2 (A_B_3, and_18_out, and_20_out, and_22_out, and_24_out, and_26_out, and_28_out, and_30_out, and_15_out);
endmodule

module _8_bit_NOT (
  input  not_A__not_B_control,
  input  [7:0] A,
  input  [7:0] B,
  output [7:0] Results
);

  wire and_1_out, and_2_out, and_3_out, and_4_out, and_5_out, and_6_out, and_7_out, and_8_out, and_9_out,
       and_10_out, and_11_out, and_12_out, and_13_out, and_14_out, and_15_out, and_16_out, not_1_out,
       not_2_out, not_3_out, not_4_out, not_5_out, not_6_out, not_7_out, not_8_out, not_9_out, not_10_out,
       not_11_out, not_12_out, not_13_out, not_14_out, not_15_out, not_16_out, not_17_out;

  not not_1 (not_1_out, A[0]);
  not not_2 (not_2_out, A[1]);
  not not_3 (not_3_out, A[2]);
  not not_4 (not_4_out, A[3]);
  not not_5 (not_5_out, A[4]);
  not not_6 (not_6_out, A[5]);
  not not_7 (not_7_out, A[6]);
  not not_8 (not_8_out, A[7]);
  not not_9 (not_9_out, not_A__not_B_control);
  not not_10 (not_10_out, B[0]);
  not not_11 (not_11_out, B[1]);
  not not_12 (not_12_out, B[2]);
  not not_13 (not_13_out, B[3]);
  not not_14 (not_14_out, B[4]);
  not not_15 (not_15_out, B[5]);
  not not_16 (not_16_out, B[6]);
  not not_17 (not_17_out, B[7]);
  and and_1 (and_1_out, not_1_out, not_9_out);
  and and_2 (and_2_out, not_2_out, not_9_out);
  and and_3 (and_3_out, not_3_out, not_9_out);
  and and_4 (and_4_out, not_4_out, not_9_out);
  and and_5 (and_5_out, not_5_out, not_9_out);
  and and_6 (and_6_out, not_6_out, not_9_out);
  and and_7 (and_7_out, not_7_out, not_9_out);
  and and_8 (and_8_out, not_8_out, not_9_out);
  and and_9 (and_9_out, not_10_out, not_A__not_B_control);
  and and_10 (and_10_out, not_11_out, not_A__not_B_control);
  and and_11 (and_11_out, not_12_out, not_A__not_B_control);
  and and_12 (and_12_out, not_13_out, not_A__not_B_control);
  and and_13 (and_13_out, not_14_out, not_A__not_B_control);
  and and_14 (and_14_out, not_15_out, not_A__not_B_control);
  and and_15 (and_15_out, not_16_out, not_A__not_B_control);
  and and_16 (and_16_out, not_17_out, not_A__not_B_control);
  or or_1 (Results[0], and_1_out, and_9_out);
  or or_2 (Results[1], and_2_out, and_10_out);
  or or_3 (Results[2], and_3_out, and_11_out);
  or or_4 (Results[3], and_4_out, and_12_out);
  or or_5 (Results[4], and_5_out, and_13_out);
  or or_6 (Results[5], and_6_out, and_14_out);
  or or_7 (Results[6], and_7_out, and_15_out);
  or or_8 (Results[7], and_8_out, and_16_out);
endmodule

module _8_bit_AND (
  input  [7:0] A,
  input  [7:0] B,
  output [7:0] Results
);

  and and_1 (Results[0], A[0], B[0]);
  and and_2 (Results[1], A[1], B[1]);
  and and_3 (Results[2], A[2], B[2]);
  and and_4 (Results[3], A[3], B[3]);
  and and_5 (Results[4], A[4], B[4]);
  and and_6 (Results[5], A[5], B[5]);
  and and_7 (Results[6], A[6], B[6]);
  and and_8 (Results[7], A[7], B[7]);
endmodule

module _8_bit_OR (
  input  [7:0] A,
  input  [7:0] B,
  output [7:0] Results
);

  or or_1 (Results[0], A[0], B[0]);
  or or_2 (Results[1], A[1], B[1]);
  or or_3 (Results[2], A[2], B[2]);
  or or_4 (Results[3], A[3], B[3]);
  or or_5 (Results[4], A[4], B[4]);
  or or_6 (Results[5], A[5], B[5]);
  or or_7 (Results[6], A[6], B[6]);
  or or_8 (Results[7], A[7], B[7]);
endmodule

module _8_bit_RIGHT_SHIFT (
  input  CARRY_IN,
  input  A___B_SWITCH,
  input  [7:0] A,
  input  [7:0] B,
  output FALL_OFF,
  output [7:0] Results
);

  MULTIPLEXER multiplexer_1 (.SELECTOR(A___B_SWITCH), .A(A[0]), .B(B[0]), .OUTPUT(FALL_OFF));
  MULTIPLEXER multiplexer_2 (.SELECTOR(A___B_SWITCH), .A(A[1]), .B(B[1]), .OUTPUT(Results[0]));
  MULTIPLEXER multiplexer_3 (.SELECTOR(A___B_SWITCH), .A(A[2]), .B(B[2]), .OUTPUT(Results[1]));
  MULTIPLEXER multiplexer_4 (.SELECTOR(A___B_SWITCH), .A(A[3]), .B(B[3]), .OUTPUT(Results[2]));
  MULTIPLEXER multiplexer_5 (.SELECTOR(A___B_SWITCH), .A(A[4]), .B(B[4]), .OUTPUT(Results[3]));
  MULTIPLEXER multiplexer_6 (.SELECTOR(A___B_SWITCH), .A(A[5]), .B(B[5]), .OUTPUT(Results[4]));
  MULTIPLEXER multiplexer_7 (.SELECTOR(A___B_SWITCH), .A(A[6]), .B(B[6]), .OUTPUT(Results[5]));
  MULTIPLEXER multiplexer_8 (.SELECTOR(A___B_SWITCH), .A(A[7]), .B(B[7]), .OUTPUT(Results[6]));
  // NOT_Gate not_1 is placed but not wired

  assign Results[7] = CARRY_IN;
endmodule

module _8_bit_LEFT_SHIFT (
  input  CARRY_IN,
  input  A___B_SWITCH,
  input  [7:0] A,
  input  [7:0] B,
  output [7:0] Results,
  output FALL_OFF
);

  MULTIPLEXER multiplexer_1 (.SELECTOR(A___B_SWITCH), .A(A[0]), .B(B[0]), .OUTPUT(Results[1]));
  MULTIPLEXER multiplexer_2 (.SELECTOR(A___B_SWITCH), .A(A[1]), .B(B[1]), .OUTPUT(Results[2]));
  MULTIPLEXER multiplexer_3 (.SELECTOR(A___B_SWITCH), .A(A[2]), .B(B[2]), .OUTPUT(Results[3]));
  MULTIPLEXER multiplexer_4 (.SELECTOR(A___B_SWITCH), .A(A[3]), .B(B[3]), .OUTPUT(Results[4]));
  MULTIPLEXER multiplexer_5 (.SELECTOR(A___B_SWITCH), .A(A[4]), .B(B[4]), .OUTPUT(Results[5]));
  MULTIPLEXER multiplexer_6 (.SELECTOR(A___B_SWITCH), .A(A[5]), .B(B[5]), .OUTPUT(Results[6]));
  MULTIPLEXER multiplexer_7 (.SELECTOR(A___B_SWITCH), .A(A[6]), .B(B[6]), .OUTPUT(Results[7]));
  MULTIPLEXER multiplexer_8 (.SELECTOR(A___B_SWITCH), .A(A[7]), .B(B[7]), .OUTPUT(FALL_OFF));

  assign Results[0] = CARRY_IN;
endmodule
